# Fritzing sketch SimGameController (saved by Fritzing 0.9.4)
breadboards: 4

parts:
  R1 = Slide Potentiometer [maximum_resistance=100kΩ]
  R2 = Slide Potentiometer [maximum_resistance=100kΩ]
  R3 = Slide Potentiometer [maximum_resistance=100kΩ]
  Composant1 = Arduino Due (Rev2b)
  Composant2 = Thumb Joystick
  Composant3 = Thumb Joystick
  Composant4 = Thumb Joystick  # not connected
  Composant5 = LCD1602-I2C  # not connected
  S1 = Round Pushbutton  # not connected
  S2 = Round Pushbutton  # not connected
  S3 = Round Pushbutton  # not connected
  S4 = Round Pushbutton  # not connected
  S5 = Round Pushbutton  # not connected
  S6 = Round Pushbutton  # not connected
  S7 = Round Pushbutton  # not connected
  S8 = Round Pushbutton  # not connected
  X1 = USB Connectors [package=usb-microb]
  Toggle_2 = Taiway 100-SP-X-T1 SPDT Miniature Toggle Switch [part_number=100-SP-X-T1-0-0-B1-M1 package=THT]
  Toggle_3 = Taiway 100-SP-X-T1 SPDT Miniature Toggle Switch [part_number=100-SP-X-T1-0-0-B1-M1 package=THT]
  Toggle_4 = Taiway 100-SP-X-T1 SPDT Miniature Toggle Switch [part_number=100-SP-X-T1-0-0-B1-M1 package=THT]
  Toggle_1 = Taiway 100-SP-X-T1 SPDT Miniature Toggle Switch [part_number=100-SP-X-T1-0-0-B1-M1 package=THT]
  Button_2 = Round Pushbutton
  Button_1 = Round Pushbutton
  sideAxe1 = Rotary Encoder [package=THT]
  sideAxe2 = Rotary Encoder [package=THT]
  Button_3 = Round Pushbutton
  J3 = Camdenboss CTB0158-10 [part_number=CTB0158-10 package=THT]
  J4 = Camdenboss CTB0158-11 [part_number=CTB0158-11 package=THT]
  R4 = Resistor [tolerance=±5% resistance=10k package=THT]
  R5 = Resistor [tolerance=±5% resistance=10k package=THT]
  R6 = Resistor [tolerance=±5% resistance=10k package=THT]
  R7 = Resistor [tolerance=±5% resistance=10k package=THT]
  R8 = Resistor [tolerance=±5% resistance=10k package=THT]
  R9 = Resistor [tolerance=±5% resistance=10k package=THT]
  R10 = Resistor [tolerance=±5% resistance=10k package=THT]
  R11 = Resistor [tolerance=±5% resistance=10k package=THT]
  R12 = Resistor [tolerance=±5% resistance=10k package=THT]
  R13 = Resistor [tolerance=±5% resistance=10k package=THT]
  R14 = Resistor [tolerance=±5% resistance=10k package=THT]
  R15 = Resistor [tolerance=±5% resistance=10k package=THT]
  R16 = Resistor [tolerance=±5% resistance=10k package=THT]
  R17 = Resistor [tolerance=±5% resistance=10k package=THT]
  R18 = Resistor [tolerance=±5% resistance=10k package=THT]
  R19 = Resistor [tolerance=±5% resistance=10k package=THT]
  R20 = Resistor [tolerance=±5% resistance=10k package=THT]
  R21 = Resistor [tolerance=±5% resistance=10k package=THT]
  R22 = Resistor [tolerance=±5% resistance=10k package=THT]
  R23 = Resistor [tolerance=±5% resistance=10k package=THT]
  R24 = Resistor [tolerance=±5% resistance=10k package=THT]
  R25 = Resistor [tolerance=±5% resistance=10k package=THT]
  R26 = Resistor [tolerance=±5% resistance=10k package=THT]
  R27 = Resistor [tolerance=±5% resistance=10k package=THT]
  Button_4 = Round Pushbutton
  Button_5 = Round Pushbutton  # not connected
  Button_6 = Round Pushbutton  # not connected
  J5 = Camdenboss CTB0158-11 [part_number=CTB0158-11 package=THT]
  GRAPH_1 = LED_BARGRAPH_10 [package=led_bargaph_10]
  buttonUp = Round Pushbutton
  buttonLeft = Round Pushbutton
  buttonRight = Round Pushbutton
  buttonDown = Round Pushbutton
  buttonSelect = Round Pushbutton
  S9 = Round Pushbutton
  J6 = Camdenboss CTB0158-11 [part_number=CTB0158-11 package=THT]
  U1 = 74HC595 [package="DIP16 [THT]"]
  U2 = 74HC595 [package="DIP16 [THT]"]
  GRAPH_3 = LED_BARGRAPH_10 [package=led_bargaph_10]
  U3 = 74HC595 [package="DIP16 [THT]"]
  R28 = Resistor [tolerance=±5% resistance=220 package=THT]
  R29 = Resistor [tolerance=±5% resistance=220 package=THT]
  R30 = Resistor [tolerance=±5% resistance=220 package=THT]
  R31 = Resistor [tolerance=±5% resistance=220 package=THT]
  R32 = Resistor [tolerance=±5% resistance=220 package=THT]
  R33 = Resistor [tolerance=±5% resistance=220 package=THT]
  R34 = Resistor [tolerance=±5% resistance=220 package=THT]
  R35 = Resistor [tolerance=±5% resistance=220 package=THT]
  R36 = Resistor [tolerance=±5% resistance=220 package=THT]
  R37 = Resistor [tolerance=±5% resistance=220 package=THT]
  R38 = Resistor [tolerance=±5% resistance=220 package=THT]
  R39 = Resistor [tolerance=±5% resistance=220 package=THT]
  R40 = Resistor [tolerance=±5% resistance=220 package=THT]
  R41 = Resistor [tolerance=±5% resistance=220 package=THT]
  R42 = Resistor [tolerance=±5% resistance=220 package=THT]
  R43 = Resistor [tolerance=±5% resistance=220 package=THT]
  R44 = Resistor [tolerance=±5% resistance=220 package=THT]
  R45 = Resistor [tolerance=±5% resistance=220 package=THT]
  R46 = Resistor [tolerance=±5% resistance=220 package=THT]
  R47 = Resistor [tolerance=±5% resistance=220 package=THT]
  R48 = Resistor [tolerance=±5% resistance=10k package=THT]
  R49 = Resistor [tolerance=±5% resistance=10k package=THT]
  R50 = Resistor [tolerance=±5% resistance=10k package=THT]
  R51 = Resistor [tolerance=±5% resistance=10k package=THT]
  R52 = Resistor [tolerance=±5% resistance=10k package=THT]
  R53 = Resistor [tolerance=±5% resistance=10k package=THT]

nets:
  VCC: R1.leg1, R2.leg1, R3.leg1, Composant1.IOREF, Composant2.VCC, Composant3.VCC, J3.pin2, R4.Pin_0, R5.Pin_0, R6.Pin_0, R7.Pin_0, R8.Pin_0, R9.Pin_0, R10.Pin_0, R11.Pin_0, R12.Pin_0, R13.Pin_0, R14.Pin_0, R15.Pin_0, R16.Pin_0, R17.Pin_0, R18.Pin_0, R19.Pin_0, R20.Pin_0, R21.Pin_0, R22.Pin_0, R23.Pin_0, R24.Pin_0, R25.Pin_0, R26.Pin_0, R27.Pin_0, R48.Pin_0, R49.Pin_0, R50.Pin_0, R51.Pin_0, R52.Pin_0, R53.Pin_0
  N1: R1.wiper, Composant1.A6, J4.pin7
  GND: R1.leg2, R2.leg2, R3.leg2, Composant2.GND, Composant3.GND, X1.GND, Toggle_2.COM, Toggle_3.COM, Toggle_4.COM, Toggle_1.COM, Button_2.leg1, Button_1.leg1, sideAxe1.EncoderPinC, sideAxe1.SwitchPinE, sideAxe2.EncoderPinC, sideAxe2.SwitchPinE, Button_3.leg0, J3.pin1, Button_4.leg0, GRAPH_1.J_C, GRAPH_1.I_C, GRAPH_1.H_C, GRAPH_1.G_C, GRAPH_1.F_C, GRAPH_1.E_C, GRAPH_1.D_C, GRAPH_1.C_C, GRAPH_1.B_C, GRAPH_1.A_C, buttonUp.leg0, buttonLeft.leg0, buttonRight.leg0, buttonDown.leg0, buttonSelect.leg0, S9.leg0, J6.pin1, U1.GND, U1.OE, U2.GND, U2.OE, GRAPH_3.J_C, GRAPH_3.I_C, GRAPH_3.H_C, GRAPH_3.G_C, GRAPH_3.F_C, GRAPH_3.E_C, GRAPH_3.D_C, GRAPH_3.C_C, GRAPH_3.B_C, GRAPH_3.A_C, U3.GND, U3.OE
  N2: R2.wiper, Composant1.A5, J4.pin6
  N3: R3.wiper, Composant1.A4, J4.pin5
  N4: Composant1.A0, Composant2.VERT, J3.pin3
  N5: Composant1.A1, Composant2.HORZ, J3.pin4
  N6: Composant1.A2, Composant3.VERT, J3.pin8
  N7: Composant1.A3, Composant3.HORZ, J3.pin7
  N8: Composant1.D22, U1.ST_CP, U2.ST_CP, U3.ST_CP
  N9: Composant1.D23, U1.SH_CP, U2.SH_CP, U3.SH_CP
  N10: Composant1.D24, U2.DS
  N11: Composant1.D25, S9.leg1, J6.pin7, J6.pin9, R48.Pin_1
  N12: Composant1.D26, buttonSelect.leg1, J6.pin6, J6.pin8, R49.Pin_1
  N13: Composant1.D27, buttonRight.leg1, J6.pin5, R50.Pin_1
  N14: Composant1.D28, buttonLeft.leg1, J6.pin4, R51.Pin_1
  N15: Composant1.D29, buttonDown.leg1, J6.pin3, R52.Pin_1
  N16: Composant1.D30, buttonUp.leg1, J6.pin2, R53.Pin_1
  N17: Composant1.D38, Composant2.SEL, J3.pin5, R13.Pin_1
  N18: Composant1.D39, Composant3.SEL, J3.pin6, R12.Pin_1
  N19: Composant1.D40, Button_1.leg0, J4.pin4, R15.Pin_1
  N20: Composant1.D41, Button_2.leg0, J4.pin3, R14.Pin_1
  N21: Composant1.D42, sideAxe1.SwitchrPinD, R17.Pin_1, J5.pin1
  N22: Composant1.D43, sideAxe2.SwitchrPinD, R16.Pin_1, J5.pin2
  N23: Composant1.D44, R19.Pin_1, Button_4.leg1, J5.pin4
  N24: Composant1.D45, Button_3.leg1, R18.Pin_1, J5.pin3
  N25: Composant1.D46, Toggle_1.L2, J4.pin11, R21.Pin_1
  N26: Composant1.D47, Toggle_2.L2, J4.pin10, R20.Pin_1
  N27: Composant1.D48, Toggle_3.L2, J4.pin9, R23.Pin_1
  N28: Composant1.D49, Toggle_4.L2, J4.pin8, R22.Pin_1
  N29: Composant1.D50, Toggle_1.L1, J4.pin2, R25.Pin_1
  N30: Composant1.D51, Toggle_2.L1, J4.pin1, R24.Pin_1
  N31: Composant1.D52, Toggle_3.L1, J3.pin10, R27.Pin_1
  N32: Composant1.D53, Toggle_4.L1, J3.pin9, R26.Pin_1
  N33: GRAPH_1.A_A, R47.Pin_0
  N34: GRAPH_1.B_A, R46.Pin_0
  N35: GRAPH_1.C_A, R45.Pin_0
  N36: GRAPH_1.D_A, R44.Pin_0
  N37: GRAPH_1.E_A, R43.Pin_0
  N38: GRAPH_1.F_A, R42.Pin_0
  N39: GRAPH_1.G_A, R41.Pin_0
  N40: GRAPH_1.H_A, R40.Pin_0
  N41: GRAPH_1.I_A, R39.Pin_0
  N42: GRAPH_1.J_A, R38.Pin_0
  N43: U1.Q1, R38.Pin_1
  N44: U1.Q2, R37.Pin_1
  N45: U1.Q3, R36.Pin_1
  N46: U1.Q4, R35.Pin_1
  N47: U1.Q5, R34.Pin_1
  N48: U1.Q6, R33.Pin_1
  N49: U1.Q7, R32.Pin_1
  N50: U1.Q7', U3.DS
  VCC_2: U1.MR, U1.VCC, U2.MR, U2.VCC, U3.MR, U3.VCC
  N51: U1.DS, U2.Q7'
  N52: U1.Q0, R39.Pin_1
  N53: U2.Q1, R46.Pin_1
  N54: U2.Q2, R45.Pin_1
  N55: U2.Q3, R44.Pin_1
  N56: U2.Q4, R43.Pin_1
  N57: U2.Q5, R42.Pin_1
  N58: U2.Q6, R41.Pin_1
  N59: U2.Q7, R40.Pin_1
  N60: U2.Q0, R47.Pin_1
  N61: GRAPH_3.A_A, R37.Pin_0
  N62: GRAPH_3.B_A, R36.Pin_0
  N63: GRAPH_3.C_A, R35.Pin_0
  N64: GRAPH_3.D_A, R34.Pin_0
  N65: GRAPH_3.E_A, R33.Pin_0
  N66: GRAPH_3.F_A, R32.Pin_0
  N67: GRAPH_3.G_A, R31.Pin_0
  N68: GRAPH_3.H_A, R30.Pin_0
  N69: GRAPH_3.I_A, R29.Pin_0
  N70: GRAPH_3.J_A, R28.Pin_0
  N71: U3.Q1, R30.Pin_1
  N72: U3.Q2, R29.Pin_1
  N73: U3.Q3, R28.Pin_1
  N74: U3.Q0, R31.Pin_1

notes:
  Ne pas oublier 3.3V
  RIGHT SIDE
  FRONT PANNEL
  3.3 VOLT !
  Button input
  VCC
  GND
  Vertical Left
  Honrizontal Left
  BUTTON LEFT
  BUTTON RIGHT
  Honrizontal Right
  Vertical Right
  Slider 1 OUT
  Slider 2 OUT
  Slider 3 OUT
  Switch
  1    2    3    4    5    6
  7    8    9   10
  Toggle 2 Down
  Toggle 3 Down
  Toggle 4 Down
  Toggle 1 Down
  Toggle 4 UP
  Toggle 3 UP
  Toggle 2 UP
  Toggle 1 UP
  Button 2
  Button 1
  BUTTON 3
  BUTTON 4
  BUTTON 5
  BUTTON 6
  Warning 5 V
  MENU buttion

custom parts:
  LCD1602-I2C: A standard character display, usually with 2x16 characters. Comes in many colors with LCM1602 IIC attached.
  Rotary Encoder: Rotary Encoder from ALPSec11e with switch.
